# Fritzing sketch wiring (saved by Fritzing 0.9.4)

parts:
  MCU1 = Raspberry Pi Zero
  Bauteil1 = Max Power IR LED Kit

nets:
  N1: MCU1.pin_2, MCU1.pin_4, Bauteil1.VCC
  N2: MCU1.pin_6, MCU1.pin_25, Bauteil1.GND
  N3: MCU1.pin_18, Bauteil1.CONTROL
